# Fritzing sketch not (saved by Fritzing 0.9.3b)
breadboards: 1

parts:
  Bauteil1 = Arduino Uno (Rev3)
  S1 = Pushbutton [package="[THT]"]
  R1 = Resistor [tolerance=±5% resistance=10k package=THT]
  LED1 = LED - 5mm [color="Red (633nm)" package="5 mm [THT]"]
  Q1 = NPN-Transistor [package="TO92 [THT]"]
  R2 = Resistor [tolerance=±5% resistance=1k package=THT]

nets:
  N1: Bauteil1.5V, S1.Pin_3, S1.Pin_4, R2.Pin_0
  N2: Bauteil1.GND, LED1.cathode, Q1.E
  N3: S1.Pin_1, S1.Pin_2, R1.Pin_0
  N4: R1.Pin_1, Q1.B
  N5: LED1.anode, Q1.C, R2.Pin_1
