# Fritzing sketch parallel_resistor (saved by Fritzing 0.9.0b)
breadboards: 2

parts:
  Bauteil2 = Arduino Uno (Rev3)
  R4 = Resistor [tolerance=±5% resistance=100 package=THT]
  R3 = Resistor [tolerance=±5% resistance=100 package=THT]
  Bauteil3 = Arduino Uno (Rev3)
  R6 = Resistor [tolerance=±5% resistance=100 package=THT]

nets:
  N1: Bauteil2.A0, Bauteil2.5V, R4.Pin_0, R3.Pin_0
  N2: Bauteil2.GND, R4.Pin_1, R3.Pin_1
  N3: Bauteil3.A0, Bauteil3.5V, R6.Pin_0
  N4: Bauteil3.GND, R6.Pin_1
