# Fritzing sketch variable-resistor (saved by Fritzing 0.9.0b)
breadboards: 1

parts:
  Bauteil1 = Arduino Uno (Rev3)
  R1 = Rotary Potentiometer (Small) [maximum_resistance=100kΩ package=THT]
  LED1 = LED - 5mm [color="Red (633nm)" package="5 mm [THT]"]
  part = Rotary Potentiometer (Small) [maximum_resistance=100kΩ package=THT]  # not connected

nets:
  N1: Bauteil1.GND, LED1.cathode
  N2: Bauteil1.5V, R1.leg1
  N3: R1.wiper, LED1.anode

notes:
  This demonstrates what a variable resistor is and how it works.
  Warning this will kill the LED.
  Make sure you have a Multimeter to check the value of the potentiometer before applying some current to it. It should be in the maximum resistance position.
