# Fritzing sketch voltage-divider (saved by Fritzing 0.9.0b)
breadboards: 1

parts:
  R1 = Resistor [tolerance=±5% resistance=1k package=THT]
  R2 = Resistor [tolerance=±5% resistance=1k package=THT]
  LED1 = LED - 5mm [color="Red (633nm)" package="5 mm [THT]"]
  VCC1 = 4 x AAA Battery Mount
  part = 4 x AAA Battery Mount  # not connected

nets:
  N1: R1.Pin_0, LED1.cathode, VCC1.-
  N2: R1.Pin_1, R2.Pin_0, LED1.anode
  N3: R2.Pin_1, VCC1.+

notes:
  This runs the LED on 2.4V This is the upper limit for an LED. It could Kill it.:)
  See this tutorial for more infos and a resistor caculator
  https://learn.sparkfun.com/tutorials/voltage-dividers/ideal-voltage-divider
